// Logisim project exampleMachine.circ as structural Verilog: 1 circuit, main circuit main
module main (
  input  [3:0] in_1,
  input  [3:0] in_2,
  input  in_3,
  output [3:0] out_4
);

  wire clock_1_out;
  wire [3:0] adder_1_out, multiplexer_1_out;

  Register #(.width(4)) register_1 (.D(adder_1_out), .Q(out_4), .clk(clock_1_out));  // open: en, clr
  Clock clock_1 (.out(clock_1_out));
  Adder #(.width(4)) adder_1 (.a(in_2), .b(multiplexer_1_out), .out(adder_1_out));  // open: cin, cout
  Multiplexer #(.width(4)) multiplexer_1 (.in0(in_1), .in1(out_4), .out(multiplexer_1_out), .sel(in_3));  // open: en
endmodule
